# Fritzing sketch blink (saved by Fritzing 0.9.3b)
breadboards: 1

parts:
  R1 = Resistor [tolerance=±5% resistance=220 package=THT]
  LED1 = LED - 5mm [color="Red (633nm)" package="5 mm [THT]"]
  Raspberry_Pi_1 = Raspberry Pi 3 [part_number=RPI-3-V1.2]

nets:
  N1: R1.Pin_0, LED1.cathode
  N2: R1.Pin_1, Raspberry_Pi_1.GND
  N3: LED1.anode, Raspberry_Pi_1.GPIO17

notes:
  电阻 220-300欧姆
  如果二极管不亮，请调换二极管针脚，可能是正负极针脚反了
