# Fritzing sketch temperature-ds18b20 (saved by Fritzing 0.9.3b)
breadboards: 1

parts:
  Raspberry_Pi_1 = Raspberry Pi 3 [part_number=RPI-3-V1.2]
  DS1 = DS18B20 1-Wire Temperature Sensor [part_number=DS18B20]
  R1 = Resistor [tolerance=±5% resistance=10k package=THT]

nets:
  3V3: Raspberry_Pi_1.3v3, Raspberry_Pi_1.3V3, DS1.VDD, R1.Pin_0
  N1: Raspberry_Pi_1.GPIO4, DS1.DQ, R1.Pin_1
  GND: Raspberry_Pi_1.GND, DS1.GND

notes:
  请注意传感器的正反面，不要弄错了。否则会烧掉。
  电阻可以为10k 欧姆或者4.7k欧姆都可以，我用的是10k欧姆
